// Logisim project CRC.circ as structural Verilog: 3 circuits, main circuit CRC
module CRC (
  input  [7:0] A,
  input  [3:0] B,
  output [10:0] C
);

  wire [10:0] bit_extender_1_out, shifter_2_out, \被除数 , \除一次_1_新被除数 , \除一次_2_新被除数 , \除一次_3_新被除数 ,
       \除一次_4_新被除数 , \除一次_5_新被除数 , \除一次_6_新被除数 , \除一次_7_新被除数 , \除一次_8_新被除数 ;

  // Probe on \除一次_1_新被除数 
  assign bit_extender_1_out = {{3{1'b0}}, A};  // Bit_Extender bit_extender_1
  \除一次  \u_除一次_1  (.\被除数 (\被除数 ), .\除数 (B), .\新被除数 (\除一次_1_新被除数 ));
  Shifter #(.width(11)) shifter_1 (.in(bit_extender_1_out), .\dist (4'b0011), .out(\被除数 ));
  // Probe on \除一次_2_新被除数 
  \除一次  \u_除一次_2  (.\被除数 (\除一次_1_新被除数 ), .\除数 (B), .\新被除数 (\除一次_2_新被除数 ));
  // Probe on \除一次_3_新被除数 
  \除一次  \u_除一次_3  (.\被除数 (\除一次_2_新被除数 ), .\除数 (B), .\新被除数 (\除一次_3_新被除数 ));
  // Probe on \除一次_4_新被除数 
  \除一次  \u_除一次_4  (.\被除数 (\除一次_3_新被除数 ), .\除数 (B), .\新被除数 (\除一次_4_新被除数 ));
  // Probe on \除一次_5_新被除数 
  \除一次  \u_除一次_5  (.\被除数 (\除一次_4_新被除数 ), .\除数 (B), .\新被除数 (\除一次_5_新被除数 ));
  \除一次  \u_除一次_6  (.\被除数 (\除一次_5_新被除数 ), .\除数 (B), .\新被除数 (\除一次_6_新被除数 ));
  // Probe on \除一次_8_新被除数 
  \除一次  \u_除一次_7  (.\被除数 (\除一次_6_新被除数 ), .\除数 (B), .\新被除数 (\除一次_7_新被除数 ));
  \除一次  \u_除一次_8  (.\被除数 (\除一次_7_新被除数 ), .\除数 (B), .\新被除数 (\除一次_8_新被除数 ));
  Shifter #(.width(11), .shift("lr")) shifter_2 (.in(\除一次_8_新被除数 ), .\dist (4'b1000), .out(shifter_2_out));
  assign C = shifter_2_out | \被除数 ;  // OR_Gate or_1, 11 bits wide
endmodule

module \四位除法器  (
  input  [3:0] \被除数 ,
  input  [3:0] \除数 ,
  output [3:0] \输出 
);

  wire \最高位 ;
  wire [3:0] shifter_1_out, xor_1_out;

  Shifter #(.width(4), .shift("lr")) shifter_1 (.in(\被除数 ), .\dist (2'b11), .out(shifter_1_out));
  assign xor_1_out = \被除数  ^ \除数 ;  // XOR_Gate xor_1, 4 bits wide
  Bit_Extender #(.in_width(4), .out_width(1)) bit_extender_1 (.in(shifter_1_out), .out(\最高位 ));
  Multiplexer #(.width(4)) multiplexer_1 (.in0(\被除数 ), .in1(xor_1_out), .out(\输出 ), .sel(\最高位 ));  // open: en
endmodule

module \除一次  (
  input  [10:0] \被除数 ,
  input  [3:0] \除数 ,
  output [10:0] \新被除数 
);

  wire [3:0] bit_extender_1_out, \四位除法器_1_输出 ;
  wire [10:0] and_1_out, bit_extender_2_out, or_1_out, shifter_1_out, shifter_2_out;

  Shifter #(.width(11), .shift("lr")) shifter_1 (.in(\被除数 ), .\dist (4'b0111), .out(shifter_1_out));
  // Probe on \四位除法器_1_输出 
  Bit_Extender #(.in_width(11), .out_width(4)) bit_extender_1 (.in(shifter_1_out), .out(bit_extender_1_out));
  \四位除法器  \u_四位除法器_1  (.\被除数 (bit_extender_1_out), .\除数 (\除数 ), .\输出 (\四位除法器_1_输出 ));
  assign bit_extender_2_out = {{7{1'b0}}, \四位除法器_1_输出 };  // Bit_Extender bit_extender_2
  Shifter #(.width(11)) shifter_2 (.in(bit_extender_2_out), .\dist (4'b0111), .out(shifter_2_out));
  // Probe on shifter_2_out
  // Probe on and_1_out
  assign and_1_out = 11'h7f & \被除数 ;  // AND_Gate and_1, 11 bits wide
  assign or_1_out = and_1_out | shifter_2_out;  // OR_Gate or_1, 11 bits wide
  Shifter #(.width(11)) shifter_3 (.in(or_1_out), .\dist (4'b0001), .out(\新被除数 ));
endmodule
