// Logisim project FSM.circ as structural Verilog: 3 circuits, main circuit fsm
module fsm (
  input  [1:0] In,
  input  CLR,
  output out_3
);

  wire clock_1_out;
  wire [1:0] multiplexer_1_out, register_1_q, \状态转换_1_o2 ;

  // Probe on \状态转换_1_o2 
  \状态转换  \u_状态转换_1  (
    .s1(register_1_q[1]), .s2(register_1_q[0]), .i1(In[1]), .i2(In[0]), .o1(\状态转换_1_o2 [1]),
    .o2(\状态转换_1_o2 [0]));
  Multiplexer #(.width(2)) multiplexer_1 (
    .in0(\状态转换_1_o2 ), .in1(2'b00), .out(multiplexer_1_out), .sel(CLR));  // open: en
  Register #(.width(2)) register_1 (.D(multiplexer_1_out), .Q(register_1_q), .clk(clock_1_out));  // open: en, clr
  Clock clock_1 (.out(clock_1_out));
  // Probe on register_1_q
  \状态输出  \u_状态输出_1  (.s1(register_1_q[1]), .s2(register_1_q[0]), .i1(In[1]), .i2(In[0]), .o(out_3));
endmodule

module \状态转换  (
  input  s1,
  input  s2,
  input  i1,
  input  i2,
  output o1,
  output o2
);

  wire and_1_out, and_2_out, and_3_out, and_4_out, and_5_out, not_1_out, not_2_out, not_3_out, not_4_out,
       not_5_out, not_6_out, not_7_out, not_8_out, not_9_out;

  not not_1 (not_1_out, s1);
  and and_1 (and_1_out, not_1_out, s2, not_2_out);
  not not_2 (not_2_out, i2);
  not not_3 (not_3_out, s2);
  and and_2 (and_2_out, s1, not_3_out, not_4_out);
  not not_4 (not_4_out, i2);
  not not_5 (not_5_out, s1);
  not not_6 (not_6_out, i1);
  and and_3 (and_3_out, not_5_out, not_6_out, i2);
  not not_7 (not_7_out, i1);
  and and_4 (and_4_out, s2, not_7_out, i2);
  and and_5 (and_5_out, s1, not_8_out, not_9_out);
  not not_8 (not_8_out, s2);
  not not_9 (not_9_out, i2);
  or or_1 (o1, and_1_out, and_2_out);
  or or_2 (o2, and_3_out, and_4_out, and_5_out);
endmodule

module \状态输出  (
  input  s1,
  input  s2,
  input  i1,
  input  i2,
  output o
);

  wire not_1_out, not_2_out;

  not not_1 (not_1_out, s2);
  and and_1 (o, s1, not_1_out, not_2_out);
  not not_2 (not_2_out, i2);
endmodule
