// Logisim project GRF.circ as structural Verilog: 3 circuits, main circuit grf
module grf (
  input  clk,
  input  reset,
  input  WE,
  input  [4:0] A1,
  input  [4:0] A2,
  input  [31:0] WD,
  input  [4:0] A3,
  output [31:0] RD2,
  output [31:0] RD1
);

  wire e1, e2, e3, e4, e5, e6, e7, e8;
  wire [1:0] \RD1个数 , \RD2个数 , \位置判定_3_个数 ;
  wire [2:0] \RD1组数 , \RD2组数 , \组数 ;
  wire [31:0] _11, _12, _13, _14, _15, _16, _17, _18, _21, _22, _23, _24, _25, _26, _27, _28,
       demultiplexer_1_out0, demultiplexer_1_out1, demultiplexer_1_out2, demultiplexer_1_out3,
       demultiplexer_1_out4, demultiplexer_1_out5, demultiplexer_1_out6, demultiplexer_1_out7;

  \位置判定  \u_位置判定_1  (.\位置输入 (A1), .\组数 (\RD1组数 ), .\个数 (\RD1个数 ));
  \位置判定  \u_位置判定_2  (.\位置输入 (A2), .\组数 (\RD2组数 ), .\个数 (\RD2个数 ));
  Demultiplexer #(.select(3), .width(32)) demultiplexer_1 (
    .out0(demultiplexer_1_out0), .out1(demultiplexer_1_out1), .out2(demultiplexer_1_out2),
    .out3(demultiplexer_1_out3), .out4(demultiplexer_1_out4), .out5(demultiplexer_1_out5),
    .out6(demultiplexer_1_out6), .out7(demultiplexer_1_out7), .in(WD), .sel(\组数 ));  // open: en
  \位置判定  \u_位置判定_3  (.\位置输入 (A3), .\组数 (\组数 ), .\个数 (\位置判定_3_个数 ));
  Multiplexer #(.select(3), .width(32)) multiplexer_1 (
    .in0(_11), .in1(_12), .in2(_13), .in3(_14), .in4(_15), .in5(_16), .in6(_17), .in7(_18), .out(RD1),
    .sel(\RD1组数 ));  // open: en
  Multiplexer #(.select(3), .width(32)) multiplexer_2 (
    .in0(_21), .in1(_22), .in2(_23), .in3(_24), .in4(_25), .in5(_26), .in6(_27), .in7(_28), .out(RD2),
    .sel(\RD2组数 ));  // open: en
  \小组  \u_小组_1  (
    .\输入 (demultiplexer_1_out0), .\输入选择 (\位置判定_3_个数 ), .\使能 (e1), .\时钟 (clk), .\复位 (reset), .\输出1 (_11),
    .\输出选择1 (\RD1个数 ), .\输出2 (_21), .\输出选择2 (\RD2个数 ));
  \小组  \u_小组_2  (
    .\输入 (demultiplexer_1_out1), .\输入选择 (\位置判定_3_个数 ), .\使能 (e2), .\时钟 (clk), .\复位 (reset), .\输出1 (_12),
    .\输出选择1 (\RD1个数 ), .\输出2 (_22), .\输出选择2 (\RD2个数 ));
  \小组  \u_小组_3  (
    .\输入 (demultiplexer_1_out2), .\输入选择 (\位置判定_3_个数 ), .\使能 (e3), .\时钟 (clk), .\复位 (reset), .\输出1 (_13),
    .\输出选择1 (\RD1个数 ), .\输出2 (_23), .\输出选择2 (\RD2个数 ));
  \小组  \u_小组_4  (
    .\输入 (demultiplexer_1_out3), .\输入选择 (\位置判定_3_个数 ), .\使能 (e4), .\时钟 (clk), .\复位 (reset), .\输出1 (_14),
    .\输出选择1 (\RD1个数 ), .\输出2 (_24), .\输出选择2 (\RD2个数 ));
  \小组  \u_小组_5  (
    .\输入 (demultiplexer_1_out4), .\输入选择 (\位置判定_3_个数 ), .\使能 (e5), .\时钟 (clk), .\复位 (reset), .\输出1 (_15),
    .\输出选择1 (\RD1个数 ), .\输出2 (_25), .\输出选择2 (\RD2个数 ));
  \小组  \u_小组_6  (
    .\输入 (demultiplexer_1_out5), .\输入选择 (\位置判定_3_个数 ), .\使能 (e6), .\时钟 (clk), .\复位 (reset), .\输出1 (_16),
    .\输出选择1 (\RD1个数 ), .\输出2 (_26), .\输出选择2 (\RD2个数 ));
  \小组  \u_小组_7  (
    .\输入 (demultiplexer_1_out6), .\输入选择 (\位置判定_3_个数 ), .\使能 (e7), .\时钟 (clk), .\复位 (reset), .\输出1 (_17),
    .\输出选择1 (\RD1个数 ), .\输出2 (_27), .\输出选择2 (\RD2个数 ));
  \小组  \u_小组_8  (
    .\输入 (demultiplexer_1_out7), .\输入选择 (\位置判定_3_个数 ), .\使能 (e8), .\时钟 (clk), .\复位 (reset), .\输出1 (_18),
    .\输出选择1 (\RD1个数 ), .\输出2 (_28), .\输出选择2 (\RD2个数 ));
  Demultiplexer #(.select(3)) demultiplexer_2 (
    .out0(e1), .out1(e2), .out2(e3), .out3(e4), .out4(e5), .out5(e6), .out6(e7), .out7(e8), .in(WE),
    .sel(\组数 ));  // open: en
endmodule

module \小组  (
  input  [31:0] \输入 ,
  input  [1:0] \输入选择 ,
  input  [1:0] \输出选择1 ,
  input  \使能 ,
  input  \时钟 ,
  input  \复位 ,
  input  [1:0] \输出选择2 ,
  output [31:0] \输出1 ,
  output [31:0] \输出2 
);

  wire demultiplexer_2_out0, demultiplexer_2_out1, demultiplexer_2_out2, demultiplexer_2_out3;
  wire [31:0] demultiplexer_1_out0, demultiplexer_1_out1, demultiplexer_1_out2, demultiplexer_1_out3,
       register_1_q, register_2_q, register_3_q, register_4_q;

  Demultiplexer #(.select(2), .width(32)) demultiplexer_1 (
    .out0(demultiplexer_1_out0), .out1(demultiplexer_1_out1), .out2(demultiplexer_1_out2),
    .out3(demultiplexer_1_out3), .in(\输入 ), .sel(\输入选择 ));  // open: en
  Demultiplexer #(.select(2)) demultiplexer_2 (
    .out0(demultiplexer_2_out0), .out1(demultiplexer_2_out1), .out2(demultiplexer_2_out2),
    .out3(demultiplexer_2_out3), .in(\使能 ), .sel(\输入选择 ));  // open: en
  Register #(.width(32)) register_1 (
    .D(demultiplexer_1_out0), .en(demultiplexer_2_out0), .Q(register_1_q), .clk(\时钟 ), .clr(\复位 ));
  Register #(.width(32)) register_2 (
    .D(demultiplexer_1_out1), .en(demultiplexer_2_out1), .Q(register_2_q), .clk(\时钟 ), .clr(\复位 ));
  Register #(.width(32)) register_3 (
    .D(demultiplexer_1_out2), .en(demultiplexer_2_out2), .Q(register_3_q), .clk(\时钟 ), .clr(\复位 ));
  Register #(.width(32)) register_4 (
    .D(demultiplexer_1_out3), .en(demultiplexer_2_out3), .Q(register_4_q), .clk(\时钟 ), .clr(\复位 ));
  Multiplexer #(.select(2), .width(32)) multiplexer_1 (
    .in0(register_1_q), .in1(register_2_q), .in2(register_3_q), .in3(register_4_q), .out(\输出2 ), .sel(\输出选择2 ));  // open: en
  Multiplexer #(.select(2), .width(32)) multiplexer_2 (
    .in0(register_1_q), .in1(register_2_q), .in2(register_3_q), .in3(register_4_q), .out(\输出1 ), .sel(\输出选择1 ));  // open: en
endmodule

module \位置判定  (
  input  [4:0] \位置输入 ,
  output [2:0] \组数 ,
  output [1:0] \个数 
);

  wire [4:0] divider_1_out, divider_1_rem;

  Divider #(.width(5)) divider_1 (.a(\位置输入 ), .b(5'b00100), .out(divider_1_out), .rem(divider_1_rem));  // open: upper
  Bit_Extender #(.in_width(5), .out_width(3)) bit_extender_1 (.in(divider_1_out), .out(\组数 ));
  Bit_Extender #(.in_width(5), .out_width(2)) bit_extender_2 (.in(divider_1_rem), .out(\个数 ));
endmodule
