// Logisim project 导航.circ as structural Verilog: 3 circuits, main circuit navigation
module navigation (
  input  [1:0] dir,
  input  clk,
  input  reset,
  output arrive,
  output hit
);

  wire counter_1_q;
  wire [5:0] multiplexer_1_out, register_1_q, \状态转换_1_h ;

  // Probe on multiplexer_1_out
  \状态转换  \u_状态转换_1  (
    .a1(multiplexer_1_out[5]), .a2(multiplexer_1_out[4]), .a3(multiplexer_1_out[3]),
    .a4(multiplexer_1_out[2]), .a5(multiplexer_1_out[1]), .b1(dir[1]), .b2(dir[0]), .o1(\状态转换_1_h [5]),
    .o2(\状态转换_1_h [4]), .o3(\状态转换_1_h [3]), .o4(\状态转换_1_h [2]), .o5(\状态转换_1_h [1]), .h(\状态转换_1_h [0]));
  // Probe on \状态转换_1_h 
  // Probe on \状态转换_1_h 
  Register #(.width(6)) register_1 (.D(\状态转换_1_h ), .Q(register_1_q), .clk(clk), .clr(reset));  // open: en
  Counter #(.width(1), .max('h1), .ongoal("stay")) counter_1 (
    .Q(counter_1_q), .clk(clk), .clr(reset));  // open: load, D, count, carry
  Multiplexer #(.width(6)) multiplexer_1 (
    .in0(6'b000010), .in1(register_1_q), .out(multiplexer_1_out), .sel(counter_1_q));  // open: en
  \状态输出  \u_状态输出_1  (
    .a1(multiplexer_1_out[5]), .a2(multiplexer_1_out[4]), .a3(multiplexer_1_out[3]),
    .a4(multiplexer_1_out[2]), .a5(multiplexer_1_out[1]), .h0(multiplexer_1_out[0]), .d(arrive), .h(hit));
endmodule

module \状态转换  (
  input  a1,
  input  a2,
  input  a3,
  input  a4,
  input  a5,
  input  b1,
  input  b2,
  output o1,
  output o2,
  output o3,
  output o4,
  output o5,
  output h
);

  wire and_1_out, and_2_out, and_3_out, and_4_out, and_5_out, and_6_out, and_7_out, and_8_out, and_9_out,
       and_10_out, and_11_out, and_12_out, and_13_out, and_14_out, and_15_out, and_16_out, not_1_out,
       not_2_out, not_3_out, not_4_out, not_5_out, not_6_out, not_7_out, not_8_out, not_9_out, not_10_out,
       not_11_out, not_12_out, not_13_out, not_14_out, not_15_out, not_16_out, not_17_out, not_18_out,
       not_19_out, not_20_out, not_21_out, not_22_out, not_23_out, not_24_out, not_25_out, not_26_out,
       not_27_out, not_28_out, not_29_out, not_30_out, not_31_out, not_32_out;

  not not_1 (not_1_out, b1);
  not not_2 (not_2_out, b2);
  not not_3 (not_3_out, b1);
  not not_4 (not_4_out, a1);
  not not_5 (not_5_out, a3);
  not not_6 (not_6_out, a5);
  not not_7 (not_7_out, b1);
  not not_8 (not_8_out, b2);
  not not_9 (not_9_out, a1);
  not not_10 (not_10_out, a2);
  not not_11 (not_11_out, a5);
  not not_12 (not_12_out, b1);
  not not_13 (not_13_out, b2);
  not not_14 (not_14_out, a1);
  not not_15 (not_15_out, a2);
  not not_16 (not_16_out, a5);
  not not_17 (not_17_out, b1);
  not not_18 (not_18_out, b2);
  not not_19 (not_19_out, b2);
  not not_20 (not_20_out, b2);
  not not_21 (not_21_out, a1);
  not not_22 (not_22_out, a2);
  not not_23 (not_23_out, a4);
  not not_24 (not_24_out, b1);
  not not_25 (not_25_out, a1);
  not not_26 (not_26_out, a2);
  not not_27 (not_27_out, a4);
  not not_28 (not_28_out, b2);
  not not_29 (not_29_out, a1);
  not not_30 (not_30_out, a3);
  not not_31 (not_31_out, b1);
  not not_32 (not_32_out, b2);
  and and_1 (and_1_out, a3, not_1_out, not_2_out);
  and and_2 (and_2_out, a2, not_3_out, b2);
  and and_3 (and_3_out, not_4_out, not_5_out, not_6_out, not_7_out, not_8_out);
  and and_4 (and_4_out, a2, b1, b2);
  and and_5 (and_5_out, not_9_out, not_10_out, not_11_out, not_12_out, b2);
  and and_6 (and_6_out, a3, b1, not_13_out);
  and and_7 (and_7_out, not_14_out, not_15_out, not_16_out, b1, b2);
  and and_8 (and_8_out, a5, not_17_out, not_18_out);
  and and_9 (and_9_out, a2, b1, not_19_out);
  and and_10 (and_10_out, a5, b2);
  and and_11 (and_11_out, a5, b1);
  and and_12 (and_12_out, a4, b1, not_20_out);
  and and_13 (and_13_out, not_21_out, not_22_out, not_23_out, not_24_out, b2);
  and and_14 (and_14_out, not_25_out, not_26_out, not_27_out, b1, not_28_out);
  and and_15 (and_15_out, not_29_out, not_30_out, b1, b2);
  and and_16 (and_16_out, a2, not_31_out, not_32_out);
  or or_1 (o1, and_1_out, and_2_out);
  or or_2 (o2, and_3_out, and_4_out);
  or or_3 (o3, and_5_out, and_6_out);
  or or_4 (o4, and_7_out, and_8_out, and_9_out);
  or or_5 (o5, and_10_out, and_11_out, and_12_out, a1);
  or or_6 (h, and_13_out, and_14_out, and_15_out, and_16_out);
endmodule

module \状态输出  (
  input  a1,
  input  a2,
  input  a3,
  input  a4,
  input  a5,
  input  h0,
  output d,
  output h
);


  assign d = a1;
  assign h = h0;
endmodule
