// Logisim project CPU - 副本.circ as structural Verilog: 17 circuits, main circuit main
module main (
  input  reset,
  output [31:0] out_2,
  output [31:0] out_3,
  output out_4,
  output [4:0] out_5,
  output [31:0] out_6,
  output out_7,
  output [31:0] out_8,
  output [31:0] out_9
);

  wire ALUin_sel, branch, clk, EXT_sel, l_s_sel, PC_sel, Shift_sel, Wreg_sel, zero;
  wire [1:0] Wdata_sel;
  wire [2:0] ALU_sel;
  wire [31:0] Adder, DM, EXT, multiplexer_1_out, multiplexer_4_out, Nadd, Rdata1, Shift;

  // Probe on out_2[15:11]
  // Probe on PC_sel
  Multiplexer #(.width(32)) multiplexer_1 (.in0(Adder), .in1(Nadd), .out(multiplexer_1_out), .sel(PC_sel));  // open: en
  Multiplexer #(.width(5)) multiplexer_2 (
    .in0(out_2[20:16]), .in1(out_2[15:11]), .out(out_5), .sel(Wreg_sel));  // open: en
  Multiplexer #(.select(2), .width(32)) multiplexer_3 (
    .in0(out_8), .in1(DM), .in2(Shift), .out(out_6), .sel(Wdata_sel));  // open: in3, en
  IFU IFU (.PC_IN(multiplexer_1_out), .clk(clk), .reset(reset), .PC_OUT(out_3), .IM_OUT(out_2));
  GRF GRF (
    .Reg1(out_2[25:21]), .Reg2(out_2[20:16]), .WD(out_6), .Wreg(out_5), .RD1(Rdata1), .RD2(out_9), .clk(clk),
    .WE(out_4), .reset(reset));
  Add add_1 (.in_1(out_3), .out_4(Adder), .clk(clk), .reset(reset));
  Clock clock_1 (.out(clk));
  // Probe on out_2[31:26]
  // Probe on out_2[5:0]
  Controller controller_1 (
    .opcode(out_2[31:26]), .funct(out_2[5:0]), .Wreg_sel(Wreg_sel), .Wdata_sel(Wdata_sel),
    .ALUin_sel(ALUin_sel), .l_s_sel(l_s_sel), .W_en(out_4), .DM_en(out_7), .branch(branch), .EXT(EXT_sel),
    .Shift_sel(Shift_sel), .ALU_sel(ALU_sel));
  Multiplexer #(.width(32)) multiplexer_4 (
    .in0(out_9), .in1(EXT), .out(multiplexer_4_out), .sel(ALUin_sel));  // open: en
  ALU ALU (.in1(Rdata1), .in2(multiplexer_4_out), .ALU_sel(ALU_sel), .zero(zero), .ALU(out_8));
  Nadd u_Nadd (.in_1(Shift), .in_2(Adder), .out_3(Nadd));
  Shift u_Shift (.in_1(EXT), .Shift_sel(Shift_sel), .out_3(Shift));
  Branch u_Branch (.branch(branch), .equal(zero), .PC_sel(PC_sel));
  EXT u_EXT (.EXT_in(out_2[15:0]), .EXT_sel(EXT_sel), .EXT(EXT));
  DM u_DM (.add(out_8), .data(out_9), .DM_en(out_7), .clk(clk), .l_s_sel(l_s_sel), .reset(reset), .out(DM));

  // Other names for the same wires on the sheet: _5_0[5:0] = out_2[5:0]; Instr[31:0] = out_2;
  //   _10_6[4:0] = out_2[10:6]; _15_11[4:0] = out_2[15:11]; _20_16[4:0] = out_2[20:16]; _25_21[4:0] = out_2[25:21];
  //   _31_26[5:0] = out_2[31:26]; ALU[31:0] = out_8; MemAddr[31:0] = out_8; DM_en = out_7; MemWrite = out_7;
  //   pc[31:0] = out_3; MemData[31:0] = out_9; Rdata2[31:0] = out_9; RegAddr[4:0] = out_5; RegData[31:0] = out_6;
  //   RegWrite = out_4; W_en = out_4
endmodule

module IFU (
  input  [31:0] PC_IN,
  input  clk,
  input  reset,
  output [31:0] PC_OUT,
  output [31:0] IM_OUT
);

  wire counter_1_q, counter_2_q;
  wire [11:0] bit_extender_1_out;
  wire [31:0] divider_1_out, subtractor_1_out;

  Counter #(.width(1), .max('h1), .ongoal("stay")) counter_1 (
    .Q(counter_1_q), .clk(clk), .clr(reset));  // open: load, D, count, carry
  Multiplexer #(.width(32)) multiplexer_1 (.sel(counter_1_q));  // open: in0, in1, out, en
  Register #(.width(32)) PC (.D(PC_IN), .Q(PC_OUT), .clk(clk), .clr(reset));  // open: en
  Subtractor #(.width(32)) subtractor_1 (.a(PC_OUT), .b(32'h3000), .out(subtractor_1_out));  // open: bin, bout
  Divider #(.width(32)) divider_1 (.a(subtractor_1_out), .b(32'h4), .out(divider_1_out));  // open: upper, rem
  Bit_Extender #(.in_width(32), .out_width(12)) bit_extender_1 (.in(divider_1_out), .out(bit_extender_1_out));
  Counter #(.width(1), .max('h1), .ongoal("stay")) counter_2 (
    .Q(counter_2_q), .clk(clk), .clr(reset));  // open: load, D, count, carry
  Multiplexer #(.width(12)) multiplexer_2 (.in0({12{1'b0}}), .sel(counter_2_q));  // open: in1, out, en
  ROM #(.addrWidth(12), .dataWidth(32)) rom_1 (.addr(bit_extender_1_out), .data(IM_OUT));  // open: sel

  // Notes on the sheet:
  //   contents of rom_1 (hex, n*v repeats v):
  //   341c0000 341d0000 34013456 210820 8c010004 ac010004 3c027878 411822 3c051234 34040005 0 ac85ffff
  //   8c83ffff 10650001 1000000d 34670404 10e3000b 0 3c087777 3508ffff 80022 34001100 e65020 34080000
  //   34090001 340a0001 10a4020 1109fffe 1000ffff
endmodule

module GRF (
  input  [4:0] Reg1,
  input  [4:0] Reg2,
  input  [31:0] WD,
  input  [4:0] Wreg,
  input  clk,
  input  WE,
  input  reset,
  output [31:0] RD1,
  output [31:0] RD2
);

  wire [1:0] \grf_位置判定_3_个数 , \RD1个数 , \RD2个数 ;
  wire [2:0] \RD1组数 , \RD2组数 , \组数 ;
  wire [31:0] _11, _12, _13, _14, _15, _16, _17, _18, _21, _22, _23, _24, _25, _26, _27, _28,
       demultiplexer_1_out0, demultiplexer_1_out1, demultiplexer_1_out2, demultiplexer_1_out3,
       demultiplexer_1_out4, demultiplexer_1_out5, demultiplexer_1_out6, demultiplexer_1_out7;

  \GRF_位置判定  \grf_位置判定_1  (.\位置输入 (Reg1), .\组数 (\RD1组数 ), .\个数 (\RD1个数 ));
  \GRF_位置判定  \grf_位置判定_2  (.\位置输入 (Reg2), .\组数 (\RD2组数 ), .\个数 (\RD2个数 ));
  Demultiplexer #(.select(3), .width(32), .tristate("true")) demultiplexer_1 (
    .out0(demultiplexer_1_out0), .out1(demultiplexer_1_out1), .out2(demultiplexer_1_out2),
    .out3(demultiplexer_1_out3), .out4(demultiplexer_1_out4), .out5(demultiplexer_1_out5),
    .out6(demultiplexer_1_out6), .out7(demultiplexer_1_out7), .in(WD), .sel(\组数 ));  // open: en
  \GRF_位置判定  \grf_位置判定_3  (.\位置输入 (Wreg), .\组数 (\组数 ), .\个数 (\grf_位置判定_3_个数 ));
  Multiplexer #(.select(3), .width(32)) multiplexer_1 (
    .in0(_11), .in1(_12), .in2(_13), .in3(_14), .in4(_15), .in5(_16), .in6(_17), .in7(_18), .out(RD1),
    .sel(\RD1组数 ));  // open: en
  Multiplexer #(.select(3), .width(32)) multiplexer_2 (
    .in0(_21), .in1(_22), .in2(_23), .in3(_24), .in4(_25), .in5(_26), .in6(_27), .in7(_28), .out(RD2),
    .sel(\RD2组数 ));  // open: en
  \GRF_小组_含0  \grf_小组_含0_1  (
    .\输入 (demultiplexer_1_out0), .\输入选择 (\grf_位置判定_3_个数 ), .\使能 (WE), .\时钟 (clk), .\复位 (reset), .\输出1 (_11),
    .\输出选择1 (\RD1个数 ), .\输出2 (_21), .\输出选择2 (\RD2个数 ));
  \GRF_小组_不含0  \grf_小组_不含0_1  (
    .\输入 (demultiplexer_1_out1), .\输入选择 (\grf_位置判定_3_个数 ), .\使能 (WE), .\时钟 (clk), .\复位 (reset), .\输出1 (_12),
    .\输出选择1 (\RD1个数 ), .\输出2 (_22), .\输出选择2 (\RD2个数 ));
  \GRF_小组_不含0  \grf_小组_不含0_2  (
    .\输入 (demultiplexer_1_out2), .\输入选择 (\grf_位置判定_3_个数 ), .\使能 (WE), .\时钟 (clk), .\复位 (reset), .\输出1 (_13),
    .\输出选择1 (\RD1个数 ), .\输出2 (_23), .\输出选择2 (\RD2个数 ));
  \GRF_小组_不含0  \grf_小组_不含0_3  (
    .\输入 (demultiplexer_1_out3), .\输入选择 (\grf_位置判定_3_个数 ), .\使能 (WE), .\时钟 (clk), .\复位 (reset), .\输出1 (_14),
    .\输出选择1 (\RD1个数 ), .\输出2 (_24), .\输出选择2 (\RD2个数 ));
  \GRF_小组_不含0  \grf_小组_不含0_4  (
    .\输入 (demultiplexer_1_out4), .\输入选择 (\grf_位置判定_3_个数 ), .\使能 (WE), .\时钟 (clk), .\复位 (reset), .\输出1 (_15),
    .\输出选择1 (\RD1个数 ), .\输出2 (_25), .\输出选择2 (\RD2个数 ));
  \GRF_小组_不含0  \grf_小组_不含0_5  (
    .\输入 (demultiplexer_1_out5), .\输入选择 (\grf_位置判定_3_个数 ), .\使能 (WE), .\时钟 (clk), .\复位 (reset), .\输出1 (_16),
    .\输出选择1 (\RD1个数 ), .\输出2 (_26), .\输出选择2 (\RD2个数 ));
  \GRF_小组_不含0  \grf_小组_不含0_6  (
    .\输入 (demultiplexer_1_out6), .\输入选择 (\grf_位置判定_3_个数 ), .\使能 (WE), .\时钟 (clk), .\复位 (reset), .\输出1 (_17),
    .\输出选择1 (\RD1个数 ), .\输出2 (_27), .\输出选择2 (\RD2个数 ));
  \GRF_小组_不含0  \grf_小组_不含0_7  (
    .\输入 (demultiplexer_1_out7), .\输入选择 (\grf_位置判定_3_个数 ), .\使能 (WE), .\时钟 (clk), .\复位 (reset), .\输出1 (_18),
    .\输出选择1 (\RD1个数 ), .\输出2 (_28), .\输出选择2 (\RD2个数 ));
endmodule

module \GRF_小组_不含0  (
  input  [31:0] \输入 ,
  input  [1:0] \输入选择 ,
  input  [1:0] \输出选择1 ,
  input  \使能 ,
  input  \时钟 ,
  input  \复位 ,
  input  [1:0] \输出选择2 ,
  output [31:0] \输出1 ,
  output [31:0] \输出2 
);

  wire [31:0] demultiplexer_1_out0, demultiplexer_1_out1, demultiplexer_1_out2, demultiplexer_1_out3,
       register_1_q, register_2_q, register_3_q, register_4_q;

  Demultiplexer #(.select(2), .width(32), .tristate("true")) demultiplexer_1 (
    .out0(demultiplexer_1_out0), .out1(demultiplexer_1_out1), .out2(demultiplexer_1_out2),
    .out3(demultiplexer_1_out3), .in(\输入 ), .sel(\输入选择 ));  // open: en
  Register #(.width(32)) register_1 (.D(demultiplexer_1_out0), .en(\使能 ), .Q(register_1_q), .clk(\时钟 ), .clr(\复位 ));
  Register #(.width(32)) register_2 (.D(demultiplexer_1_out1), .en(\使能 ), .Q(register_2_q), .clk(\时钟 ), .clr(\复位 ));
  Register #(.width(32)) register_3 (.D(demultiplexer_1_out2), .en(\使能 ), .Q(register_3_q), .clk(\时钟 ), .clr(\复位 ));
  Register #(.width(32)) register_4 (.D(demultiplexer_1_out3), .en(\使能 ), .Q(register_4_q), .clk(\时钟 ), .clr(\复位 ));
  Multiplexer #(.select(2), .width(32)) multiplexer_1 (
    .in0(register_1_q), .in1(register_2_q), .in2(register_3_q), .in3(register_4_q), .out(\输出2 ), .sel(\输出选择2 ));  // open: en
  Multiplexer #(.select(2), .width(32)) multiplexer_2 (
    .in0(register_1_q), .in1(register_2_q), .in2(register_3_q), .in3(register_4_q), .out(\输出1 ), .sel(\输出选择1 ));  // open: en
endmodule

module \GRF_小组_含0  (
  input  [31:0] \输入 ,
  input  [1:0] \输入选择 ,
  input  [1:0] \输出选择1 ,
  input  \使能 ,
  input  \时钟 ,
  input  \复位 ,
  input  [1:0] \输出选择2 ,
  output [31:0] \输出1 ,
  output [31:0] \输出2 
);

  wire [31:0] demultiplexer_1_out1, demultiplexer_1_out2, demultiplexer_1_out3, register_1_q, register_2_q,
       register_3_q, register_4_q;

  Demultiplexer #(.select(2), .width(32), .tristate("true")) demultiplexer_1 (
    .out1(demultiplexer_1_out1), .out2(demultiplexer_1_out2), .out3(demultiplexer_1_out3), .in(\输入 ),
    .sel(\输入选择 ));  // open: out0, en
  Register #(.width(32)) register_1 (.D({32{1'b0}}), .en(\使能 ), .Q(register_1_q), .clk(\时钟 ), .clr(\复位 ));
  Register #(.width(32)) register_2 (.D(demultiplexer_1_out1), .en(\使能 ), .Q(register_2_q), .clk(\时钟 ), .clr(\复位 ));
  Register #(.width(32)) register_3 (.D(demultiplexer_1_out2), .en(\使能 ), .Q(register_3_q), .clk(\时钟 ), .clr(\复位 ));
  Register #(.width(32)) register_4 (.D(demultiplexer_1_out3), .en(\使能 ), .Q(register_4_q), .clk(\时钟 ), .clr(\复位 ));
  Multiplexer #(.select(2), .width(32)) multiplexer_1 (
    .in0(register_1_q), .in1(register_2_q), .in2(register_3_q), .in3(register_4_q), .out(\输出2 ), .sel(\输出选择2 ));  // open: en
  Multiplexer #(.select(2), .width(32)) multiplexer_2 (
    .in0(register_1_q), .in1(register_2_q), .in2(register_3_q), .in3(register_4_q), .out(\输出1 ), .sel(\输出选择1 ));  // open: en
endmodule

module \GRF_位置判定  (
  input  [4:0] \位置输入 ,
  output [2:0] \组数 ,
  output [1:0] \个数 
);

  wire [4:0] divider_1_out, divider_1_rem;

  Divider #(.width(5)) divider_1 (.a(\位置输入 ), .b(5'b00100), .out(divider_1_out), .rem(divider_1_rem));  // open: upper
  Bit_Extender #(.in_width(5), .out_width(3)) bit_extender_1 (.in(divider_1_out), .out(\组数 ));
  Bit_Extender #(.in_width(5), .out_width(2)) bit_extender_2 (.in(divider_1_rem), .out(\个数 ));
endmodule

module ALU (
  input  [31:0] in1,
  input  [31:0] in2,
  input  [2:0] ALU_sel,
  output zero,
  output [31:0] ALU
);

  wire [31:0] tunnel, tunnel_t, \与 , \或 ;

  Adder #(.width(32)) adder_1 (.a(in1), .b(in2), .out(tunnel));  // open: cin, cout
  Subtractor #(.width(32)) subtractor_1 (.a(in1), .b(in2), .out(tunnel_t));  // open: bin, bout
  assign \与  = in1 & in2;  // AND_Gate and_1, 32 bits wide
  assign \或  = in1 | in2;  // OR_Gate or_1, 32 bits wide
  Comparator #(.width(32)) comparator_1 (.a({32{1'b0}}), .b(tunnel_t), .eq(zero));  // open: gt, lt
  Multiplexer #(.select(3), .width(32)) multiplexer_1 (
    .in0(\与 ), .in1(\或 ), .in2(tunnel), .in6(tunnel_t), .in7({32{1'b0}}), .out(ALU), .sel(ALU_sel));  // open: in3, in4, in5, en
endmodule

module DM (
  input  [31:0] add,
  input  [31:0] data,
  input  reset,
  input  DM_en,
  input  clk,
  input  l_s_sel,
  output [31:0] out
);

  wire not_1_out;
  wire [11:0] bit_extender_1_out;

  Bit_Extender #(.in_width(32), .out_width(12)) bit_extender_1 (.in(add), .out(bit_extender_1_out));
  not not_1 (not_1_out, l_s_sel);
  RAM #(.addrWidth(12), .dataWidth(32), .bus("separate")) ram_1 (
    .addr(bit_extender_1_out), .din(data), .data(out), .str(not_1_out), .sel(DM_en), .clk(clk), .ld(l_s_sel),
    .clr(reset));
endmodule

module EXT (
  input  [15:0] EXT_in,
  input  EXT_sel,
  output [31:0] EXT
);

  wire [31:0] EXT_out, SignEXT_out;

  assign SignEXT_out = {{16{EXT_in[15]}}, EXT_in};  // Bit_Extender bit_extender_1
  assign EXT_out = {{16{1'b0}}, EXT_in};  // Bit_Extender bit_extender_2
  Multiplexer #(.width(32)) multiplexer_1 (.in0(SignEXT_out), .in1(EXT_out), .out(EXT), .sel(EXT_sel));  // open: en
endmodule

module Controller (
  input  [5:0] opcode,
  input  [5:0] funct,
  output Wreg_sel,
  output [1:0] Wdata_sel,
  output ALUin_sel,
  output l_s_sel,
  output W_en,
  output DM_en,
  output branch,
  output EXT,
  output Shift_sel,
  output [2:0] ALU_sel
);

  wire \con_和逻辑_1_alu , \con_和逻辑_1_beq , \con_和逻辑_1_lui , \con_和逻辑_1_lw , \con_和逻辑_1_ori , \con_和逻辑_1_sw ;
  wire [1:0] ALUop;

  \Con_和逻辑  \con_和逻辑_1  (
    .ori(\con_和逻辑_1_ori ), .lw(\con_和逻辑_1_lw ), .sw(\con_和逻辑_1_sw ), .beq(\con_和逻辑_1_beq ),
    .lui(\con_和逻辑_1_lui ), .op5(opcode[5]), .op4(opcode[4]), .op3(opcode[3]), .op2(opcode[2]),
    .op1(opcode[1]), .op0(opcode[0]), .ALU(\con_和逻辑_1_alu ));
  \Con_或逻辑  \con_或逻辑_1  (
    .ori(\con_和逻辑_1_ori ), .lw(\con_和逻辑_1_lw ), .sw(\con_和逻辑_1_sw ), .beq(\con_和逻辑_1_beq ),
    .lui(\con_和逻辑_1_lui ), .ALU(\con_和逻辑_1_alu ), .Wreg_sel(Wreg_sel), .Wdata(Wdata_sel),
    .ALUin_sel(ALUin_sel), .ALUop_sel(ALUop), .l_s_sel(l_s_sel), .W_en(W_en), .DM_en(DM_en), .branch(branch),
    .EXT_sel(EXT), .Shift_sel(Shift_sel));
  \Con_ALU译码  \con_alu译码_1  (
    .op1(ALUop[1]), .op0(ALUop[0]), .funct3(funct[3]), .funct2(funct[2]), .funct1(funct[1]),
    .funct0(funct[0]), .sel2(ALU_sel[2]), .sel1(ALU_sel[1]), .sel0(ALU_sel[0]));
endmodule

module \Con_和逻辑  (
  input  op5,
  input  op4,
  input  op3,
  input  op2,
  input  op1,
  input  op0,
  output ori,
  output lw,
  output sw,
  output beq,
  output lui,
  output ALU
);

  wire not_1_out, not_2_out, not_3_out, not_4_out, not_5_out, not_6_out;

  not not_1 (not_1_out, op5);
  not not_2 (not_2_out, op4);
  not not_3 (not_3_out, op3);
  not not_4 (not_4_out, op2);
  not not_5 (not_5_out, op0);
  not not_6 (not_6_out, op1);
  and u_ori (ori, not_1_out, not_2_out, op3, op2, not_6_out, op0);
  and u_lw (lw, op5, not_2_out, not_3_out, not_4_out, op1, op0);
  and u_sw (sw, op5, not_2_out, op3, not_4_out, op1, op0);
  and u_beq (beq, not_1_out, not_2_out, not_3_out, op2, not_6_out, not_5_out);
  and u_lui (lui, not_1_out, not_2_out, op3, op2, op1, op0);
  and u_ALU (ALU, not_1_out, not_2_out, not_3_out, not_4_out, not_6_out, not_5_out);
endmodule

module \Con_或逻辑  (
  input  ori,
  input  lw,
  input  sw,
  input  beq,
  input  lui,
  input  ALU,
  output Wreg_sel,
  output [1:0] Wdata,
  output ALUin_sel,
  output [1:0] ALUop_sel,
  output l_s_sel,
  output W_en,
  output DM_en,
  output branch,
  output EXT_sel,
  output Shift_sel
);

  or Wdata_sel_0 (Wdata[0], lw, sw);
  or u_ALUin_sel (ALUin_sel, ori, lw, sw);
  or or_1 (ALUop_sel[1], ALU, ori);
  or or_2 (ALUop_sel[0], beq, ori);
  or u_W_en (W_en, ALU, ori, lw, lui);
  or or_3 (DM_en, sw, lw);

  assign branch = beq;
  assign EXT_sel = ori;
  assign l_s_sel = lw;
  assign Shift_sel = lui;
  assign Wdata[1] = lui;
  assign Wreg_sel = ALU;

  // Other names for the same wires on the sheet: Wdata_sel_1 = lui
endmodule

module \Con_ALU译码  (
  input  op1,
  input  op0,
  input  funct3,
  input  funct2,
  input  funct1,
  input  funct0,
  output sel2,
  output sel1,
  output sel0
);

  wire and_1_out, and_2_out, and_3_out, and_4_out, and_5_out, and_6_out, not_1_out, not_2_out, not_3_out,
       not_4_out, not_5_out;

  not not_1 (not_1_out, op1);
  not not_2 (not_2_out, op0);
  not not_3 (not_3_out, op0);
  not not_4 (not_4_out, funct2);
  and and_1 (and_1_out, op1, funct0);
  and and_2 (and_2_out, op1, funct3);
  and and_3 (and_3_out, op1, op0);
  and and_4 (and_4_out, not_1_out, op0);
  and and_5 (and_5_out, op1, not_2_out, funct1);
  not not_5 (not_5_out, op1);
  and and_6 (and_6_out, not_3_out, not_4_out);
  or or_1 (sel0, and_1_out, and_2_out, and_3_out);
  or or_2 (sel2, and_4_out, and_5_out);
  or or_3 (sel1, not_5_out, and_6_out);
endmodule

module Shift (
  input  [31:0] in_1,
  input  Shift_sel,
  output [31:0] out_3
);

  wire [31:0] shifter_1_out, shifter_2_out;

  Shifter #(.width(32)) shifter_1 (.in(in_1), .\dist (5'b00010), .out(shifter_1_out));
  Shifter #(.width(32)) shifter_2 (.in(in_1), .\dist (5'b10000), .out(shifter_2_out));
  Multiplexer #(.width(32)) multiplexer_1 (
    .in0(shifter_1_out), .in1(shifter_2_out), .out(out_3), .sel(Shift_sel));  // open: en
endmodule

module Nadd (
  input  [31:0] in_1,
  input  [31:0] in_2,
  output [31:0] out_3
);

  Adder #(.width(32)) adder_1 (.a(in_1), .b(in_2), .out(out_3));  // open: cin, cout
endmodule

module Branch (
  input  branch,
  input  equal,
  output PC_sel
);

  and and_1 (PC_sel, branch, equal);
endmodule

module Add (
  input  [31:0] in_1,
  input  clk,
  input  reset,
  output [31:0] out_4
);

  wire counter_1_q;
  wire [31:0] adder_1_out;

  Adder #(.width(32)) adder_1 (.a(in_1), .b(32'h4), .out(adder_1_out));  // open: cin, cout
  Counter #(.width(1), .max('h1), .ongoal("stay")) counter_1 (
    .Q(counter_1_q), .clk(clk), .clr(reset));  // open: load, D, count, carry
  Multiplexer #(.width(32)) multiplexer_1 (
    .in0(32'h3000), .in1(adder_1_out), .out(out_4), .sel(counter_1_q));  // open: en
endmodule
